// Digital circuit 1x1 RAM.dig as structural Verilog
module _1x1_RAM (
  input  CLK,
  input  RS2,
  input  RS1,
  input  WS,
  input  WD,
  output RD1,
  output RD2
);

  wire multiplexer_1_out, Q;

  Multiplexer multiplexer_1 (.sel(WS), .in_0(Q), .in_1(WD), .out(multiplexer_1_out));
  D_FF d_ff_1 (.D(multiplexer_1_out), .C(CLK), .Q(Q));  // open: nQ
  and and_1 (RD1, RS1, Q);
  and and_2 (RD2, RS2, Q);
endmodule
