// Digital circuit 1x17 RAM.dig as structural Verilog
module _1x17_RAM (
  input  RS1,
  input  RS2,
  input  [16:0] WD_16_0,
  input  WS,
  input  CLK,
  output [16:0] RD1_16_0,
  output [16:0] RD2_16_0
);

  _1x1_RAM _1x1_ram_1 (.RD1(RD1_16_0[0]), .RD2(RD2_16_0[0]), .RS1(RS1), .RS2(RS2), .WS(WS), .WD(WD_16_0[0]), .CLK(CLK));
  _1x1_RAM _1x1_ram_2 (.RD1(RD1_16_0[4]), .RD2(RD2_16_0[4]), .RS1(RS1), .RS2(RS2), .WS(WS), .WD(WD_16_0[4]), .CLK(CLK));
  _1x1_RAM _1x1_ram_3 (.RD1(RD1_16_0[8]), .RD2(RD2_16_0[8]), .RS1(RS1), .RS2(RS2), .WS(WS), .WD(WD_16_0[8]), .CLK(CLK));
  _1x1_RAM _1x1_ram_4 (
    .RD1(RD1_16_0[12]), .RD2(RD2_16_0[12]), .RS1(RS1), .RS2(RS2), .WS(WS), .WD(WD_16_0[12]), .CLK(CLK));
  _1x1_RAM _1x1_ram_5 (
    .RD1(RD1_16_0[16]), .RD2(RD2_16_0[16]), .RS1(RS1), .RS2(RS2), .WS(WS), .WD(WD_16_0[16]), .CLK(CLK));
  _1x1_RAM _1x1_ram_6 (.RD1(RD1_16_0[1]), .RD2(RD2_16_0[1]), .RS1(RS1), .RS2(RS2), .WS(WS), .WD(WD_16_0[1]), .CLK(CLK));
  _1x1_RAM _1x1_ram_7 (.RD1(RD1_16_0[5]), .RD2(RD2_16_0[5]), .RS1(RS1), .RS2(RS2), .WS(WS), .WD(WD_16_0[5]), .CLK(CLK));
  _1x1_RAM _1x1_ram_8 (.RD1(RD1_16_0[9]), .RD2(RD2_16_0[9]), .RS1(RS1), .RS2(RS2), .WS(WS), .WD(WD_16_0[9]), .CLK(CLK));
  _1x1_RAM _1x1_ram_9 (
    .RD1(RD1_16_0[13]), .RD2(RD2_16_0[13]), .RS1(RS1), .RS2(RS2), .WS(WS), .WD(WD_16_0[13]), .CLK(CLK));
  _1x1_RAM _1x1_ram_10 (
    .RD1(RD1_16_0[2]), .RD2(RD2_16_0[2]), .RS1(RS1), .RS2(RS2), .WS(WS), .WD(WD_16_0[2]), .CLK(CLK));
  _1x1_RAM _1x1_ram_11 (
    .RD1(RD1_16_0[6]), .RD2(RD2_16_0[6]), .RS1(RS1), .RS2(RS2), .WS(WS), .WD(WD_16_0[6]), .CLK(CLK));
  _1x1_RAM _1x1_ram_12 (
    .RD1(RD1_16_0[10]), .RD2(RD2_16_0[10]), .RS1(RS1), .RS2(RS2), .WS(WS), .WD(WD_16_0[10]), .CLK(CLK));
  _1x1_RAM _1x1_ram_13 (
    .RD1(RD1_16_0[14]), .RD2(RD2_16_0[14]), .RS1(RS1), .RS2(RS2), .WS(WS), .WD(WD_16_0[14]), .CLK(CLK));
  _1x1_RAM _1x1_ram_14 (
    .RD1(RD1_16_0[3]), .RD2(RD2_16_0[3]), .RS1(RS1), .RS2(RS2), .WS(WS), .WD(WD_16_0[3]), .CLK(CLK));
  _1x1_RAM _1x1_ram_15 (
    .RD1(RD1_16_0[7]), .RD2(RD2_16_0[7]), .RS1(RS1), .RS2(RS2), .WS(WS), .WD(WD_16_0[7]), .CLK(CLK));
  _1x1_RAM _1x1_ram_16 (
    .RD1(RD1_16_0[11]), .RD2(RD2_16_0[11]), .RS1(RS1), .RS2(RS2), .WS(WS), .WD(WD_16_0[11]), .CLK(CLK));
  _1x1_RAM _1x1_ram_17 (
    .RD1(RD1_16_0[15]), .RD2(RD2_16_0[15]), .RS1(RS1), .RS2(RS2), .WS(WS), .WD(WD_16_0[15]), .CLK(CLK));

  // Other names for the same wires on the sheet: Q1_0 = RD1_16_0[0]; Q1_1 = RD1_16_0[1]; Q1_2 = RD1_16_0[2];
  //   Q1_3 = RD1_16_0[3]; Q1_4 = RD1_16_0[4]; Q1_5 = RD1_16_0[5]; Q1_6 = RD1_16_0[6]; Q1_7 = RD1_16_0[7];
  //   Q1_8 = RD1_16_0[8]; Q1_9 = RD1_16_0[9]; Q1_10 = RD1_16_0[10]; Q1_11 = RD1_16_0[11]; Q1_12 = RD1_16_0[12];
  //   Q1_13 = RD1_16_0[13]; Q1_14 = RD1_16_0[14]; Q1_15 = RD1_16_0[15]; Q1_16 = RD1_16_0[16]; Q2_0 = RD2_16_0[0];
  //   Q2_1 = RD2_16_0[1]; Q2_2 = RD2_16_0[2]; Q2_3 = RD2_16_0[3]; Q2_4 = RD2_16_0[4]; Q2_5 = RD2_16_0[5];
  //   Q2_6 = RD2_16_0[6]; Q2_7 = RD2_16_0[7]; Q2_8 = RD2_16_0[8]; Q2_9 = RD2_16_0[9]; Q2_10 = RD2_16_0[10];
  //   Q2_11 = RD2_16_0[11]; Q2_12 = RD2_16_0[12]; Q2_13 = RD2_16_0[13]; Q2_14 = RD2_16_0[14]; Q2_15 = RD2_16_0[15];
  //   Q2_16 = RD2_16_0[16]; D0 = WD_16_0[0]; D1 = WD_16_0[1]; D2 = WD_16_0[2]; D3 = WD_16_0[3]; D4 = WD_16_0[4];
  //   D5 = WD_16_0[5]; D6 = WD_16_0[6]; D7 = WD_16_0[7]; D8 = WD_16_0[8]; D9 = WD_16_0[9]; D10 = WD_16_0[10];
  //   D11 = WD_16_0[11]; D12 = WD_16_0[12]; D13 = WD_16_0[13]; D14 = WD_16_0[14]; D15 = WD_16_0[15];
  //   D16 = WD_16_0[16]
endmodule
