// Digital circuit 3-Bit Program Register.dig as structural Verilog
module _3_Bit_Program_Register (
  input  CLK,
  input  [2:0] I_2_0,
  output [2:0] O_2_0
);

  _1_Bit_Reg _1_bit_reg_1 (.Din(I_2_0[0]), .Sel(1'b1), .CLK(CLK), .Dout(O_2_0[0]));
  _1_Bit_Reg _1_bit_reg_2 (.Din(I_2_0[1]), .Sel(1'b1), .CLK(CLK), .Dout(O_2_0[1]));
  _1_Bit_Reg _1_bit_reg_3 (.Din(I_2_0[2]), .Sel(1'b1), .CLK(CLK), .Dout(O_2_0[2]));
endmodule
