// Digital circuit 3_Bit_Pc_Adder.dig as structural Verilog
module _3_Bit_Pc_Adder (
  input  [2:0] I_2_0,
  output [2:0] O_2_0
);

  Add #(.Bits(3)) add_1 (.a(I_2_0), .b(3'b001), .c_i(1'b0), .s(O_2_0));  // open: c_o

  // Other names for the same wires on the sheet: I[2:0] = I_2_0; O[2:0] = O_2_0
endmodule
