// Digital circuit 5 Bit ALU.dig as structural Verilog
module _5_Bit_ALU (
  input  [4:0] A_4_0,
  input  [4:0] B_4_0,
  input  [1:0] OP_1_0,
  input  CF_in,
  output CF,
  output [4:0] O_4_0,
  output ZF,
  output SF
);

  wire [2:0] f0, f1, f2;
  wire [4:0] _5_bit_add_1_s_4_0, _5_bit_and_1_o_4_0, _5_bit_shr_1_o_4_0;

  _5_Bit_AND _5_bit_and_1 (
    .A_4_0(A_4_0), .B_4_0(B_4_0), .CF(f0[0]), .ZF(f0[1]), .SF(f0[2]), .O_4_0(_5_bit_and_1_o_4_0));
  _5_Bit_ADD _5_bit_add_1 (
    .B_4_0(B_4_0), .A_4_0(A_4_0), .S_4_0(_5_bit_add_1_s_4_0), .CF(f1[0]), .ZF(f1[1]), .SF(f1[2]));
  _5_Bit_SHR _5_bit_shr_1 (
    .A_4_0(A_4_0), .B_4_0(B_4_0), .CF_in(CF_in), .O_4_0(_5_bit_shr_1_o_4_0), .CF(f2[0]), .ZF(f2[1]),
    .SF(f2[2]));
  Multiplexer #(.Bits(3), .Selector_Bits(2)) multiplexer_1 (
    .sel(OP_1_0), .in_0(f0), .in_1(f1), .in_2(f2), .in_3(3'b000), .out({SF, ZF, CF}));
  Multiplexer #(.Selector_Bits(2), .Bits(5)) multiplexer_2 (
    .sel(OP_1_0), .in_0(_5_bit_and_1_o_4_0), .in_1(_5_bit_add_1_s_4_0), .in_2(_5_bit_shr_1_o_4_0),
    .in_3({5{1'b0}}), .out(O_4_0));

  // Other names for the same wires on the sheet: A[4:0] = A_4_0; B[4:0] = B_4_0; O[4:0] = O_4_0; op[1:0] = OP_1_0
endmodule
