// Digital circuit 5-Bit ADD.dig as structural Verilog
module _5_Bit_ADD (
  input  [4:0] B_4_0,
  input  [4:0] A_4_0,
  output [4:0] S_4_0,
  output CF,
  output ZF,
  output SF
);

  wire fa2_2_cout, fa2_3_cout, fa2_4_cout, fa2_5_cout;

  FA2 fa2_1 (.B(B_4_0[4]), .A(A_4_0[4]), .Cin(fa2_2_cout), .Cout(CF), .S(S_4_0[4]));
  FA2 fa2_2 (.B(B_4_0[3]), .A(A_4_0[3]), .Cin(fa2_3_cout), .Cout(fa2_2_cout), .S(S_4_0[3]));
  FA2 fa2_3 (.B(B_4_0[2]), .A(A_4_0[2]), .Cin(fa2_4_cout), .Cout(fa2_3_cout), .S(S_4_0[2]));
  FA2 fa2_4 (.B(B_4_0[1]), .A(A_4_0[1]), .Cin(fa2_5_cout), .Cout(fa2_4_cout), .S(S_4_0[1]));
  FA2 fa2_5 (.B(B_4_0[0]), .A(A_4_0[0]), .Cin(1'b0), .Cout(fa2_5_cout), .S(S_4_0[0]));
  and and_1 (ZF, ~S_4_0[0], ~S_4_0[1], ~S_4_0[2], ~S_4_0[3], ~S_4_0[4]);  // And

  assign SF = S_4_0[4];

  // Other names for the same wires on the sheet: Cout = CF
endmodule
