// Digital circuit 5-Bit Register Set with 4 Register.dig as structural Verilog
module _5_Bit_Register_Set_with_4_Register (
  input  [1:0] WR_1_0,
  input  WE,
  input  [4:0] WRD_4_0,
  input  CLK,
  input  [1:0] Ra_1_0,
  input  [1:0] Rb_1_0,
  output [4:0] A_4_0,
  output [4:0] B_4_0
);

  wire A0, A1, A2, A3, D0, D1, D2, D3;
  wire [4:0] R0, R1, R2, R3;

  and and_1 (D3, A3, WE);
  Decoder #(.Selector_Bits(2)) decoder_1 (.sel(WR_1_0), .out_0(A0), .out_1(A1), .out_2(A2), .out_3(A3));
  and and_2 (D2, A2, WE);
  and and_3 (D1, A1, WE);
  and and_4 (D0, A0, WE);
  _5_Bit_Register _5_bit_register_1 (.CLK(CLK), .A_4_0(WRD_4_0), .Sel(D3), .Dout_4_0(R3));
  _5_Bit_Register _5_bit_register_2 (.CLK(CLK), .A_4_0(WRD_4_0), .Sel(D2), .Dout_4_0(R2));
  _5_Bit_Register _5_bit_register_3 (.CLK(CLK), .A_4_0(WRD_4_0), .Sel(D1), .Dout_4_0(R1));
  _5_Bit_Register _5_bit_register_4 (.CLK(CLK), .A_4_0(WRD_4_0), .Sel(D0), .Dout_4_0(R0));
  Multiplexer #(.Selector_Bits(2), .Bits(5)) multiplexer_1 (
    .sel(Ra_1_0), .in_0(R0), .in_1(R1), .in_2(R2), .in_3(R3), .out(A_4_0));
  Multiplexer #(.Selector_Bits(2), .Bits(5)) multiplexer_2 (
    .sel(Rb_1_0), .in_0(R0), .in_1(R1), .in_2(R2), .in_3(R3), .out(B_4_0));

  // Other names for the same wires on the sheet: o1[4:0] = A_4_0; o2[4:0] = B_4_0; r[1:0] = Rb_1_0;
  //   r1_t[1:0] = Ra_1_0; wr[1:0] = WR_1_0; wrd[4:0] = WRD_4_0
endmodule
