// Digital circuit 5-Bit Register.dig as structural Verilog
module _5_Bit_Register (
  input  CLK,
  input  [4:0] A_4_0,
  input  Sel,
  output [4:0] Dout_4_0
);

  _1_Bit_Register _1_bit_register_1 (.Din(A_4_0[0]), .Sel(Sel), .CLK(CLK), .Dout(Dout_4_0[0]));
  _1_Bit_Register _1_bit_register_2 (.Din(A_4_0[1]), .Sel(Sel), .CLK(CLK), .Dout(Dout_4_0[1]));
  _1_Bit_Register _1_bit_register_3 (.Din(A_4_0[2]), .Sel(Sel), .CLK(CLK), .Dout(Dout_4_0[2]));
  _1_Bit_Register _1_bit_register_4 (.Din(A_4_0[3]), .Sel(Sel), .CLK(CLK), .Dout(Dout_4_0[3]));
  _1_Bit_Register _1_bit_register_5 (.Din(A_4_0[4]), .Sel(Sel), .CLK(CLK), .Dout(Dout_4_0[4]));
endmodule
