// Digital circuit 5-Bit SHR.dig as structural Verilog
module _5_Bit_SHR (
  input  [4:0] A_4_0,
  input  [4:0] B_4_0,
  input  CF_in,
  output [4:0] O_4_0,
  output CF,
  output ZF,
  output SF
);

  wire CF_tmp, comparator_1_gt;

  Comparator #(.Bits(5)) comparator_1 (.a(B_4_0), .b(5'b00101), .gt(comparator_1_gt));  // open: eq, lt
  Multiplexer multiplexer_1 (.sel(comparator_1_gt), .in_0(CF_tmp), .in_1(1'b0), .out(CF));
  Multiplexer #(.Selector_Bits(3)) multiplexer_2 (
    .sel(B_4_0[2:0]), .in_0(CF_in), .in_1(A_4_0[0]), .in_2(A_4_0[1]), .in_3(A_4_0[2]), .in_4(A_4_0[3]),
    .in_5(A_4_0[4]), .in_6(1'b0), .in_7(1'b0), .out(CF_tmp));
  Multiplexer #(.Selector_Bits(5)) multiplexer_3 (
    .sel(B_4_0), .in_0(A_4_0[4]), .in_1(1'b0), .in_2(1'b0), .in_3(1'b0), .in_4(1'b0), .in_5(1'b0),
    .in_6(1'b0), .in_7(1'b0), .in_8(1'b0), .in_9(1'b0), .in_10(1'b0), .in_11(1'b0), .in_12(1'b0),
    .in_13(1'b0), .in_14(1'b0), .in_15(1'b0), .in_16(1'b0), .in_17(1'b0), .in_18(1'b0), .in_19(1'b0),
    .in_20(1'b0), .in_21(1'b0), .in_22(1'b0), .in_23(1'b0), .in_24(1'b0), .in_25(1'b0), .in_26(1'b0),
    .in_27(1'b0), .in_28(1'b0), .in_29(1'b0), .in_30(1'b0), .in_31(1'b0), .out(O_4_0[4]));
  Multiplexer #(.Selector_Bits(5)) multiplexer_4 (
    .sel(B_4_0), .in_0(A_4_0[3]), .in_1(A_4_0[4]), .in_2(1'b0), .in_3(1'b0), .in_4(1'b0), .in_5(1'b0),
    .in_6(1'b0), .in_7(1'b0), .in_8(1'b0), .in_9(1'b0), .in_10(1'b0), .in_11(1'b0), .in_12(1'b0),
    .in_13(1'b0), .in_14(1'b0), .in_15(1'b0), .in_16(1'b0), .in_17(1'b0), .in_18(1'b0), .in_19(1'b0),
    .in_20(1'b0), .in_21(1'b0), .in_22(1'b0), .in_23(1'b0), .in_24(1'b0), .in_25(1'b0), .in_26(1'b0),
    .in_27(1'b0), .in_28(1'b0), .in_29(1'b0), .in_30(1'b0), .in_31(1'b0), .out(O_4_0[3]));
  Multiplexer #(.Selector_Bits(5)) multiplexer_5 (
    .sel(B_4_0), .in_0(A_4_0[2]), .in_1(A_4_0[3]), .in_2(A_4_0[4]), .in_3(1'b0), .in_4(1'b0), .in_5(1'b0),
    .in_6(1'b0), .in_7(1'b0), .in_8(1'b0), .in_9(1'b0), .in_10(1'b0), .in_11(1'b0), .in_12(1'b0),
    .in_13(1'b0), .in_14(1'b0), .in_15(1'b0), .in_16(1'b0), .in_17(1'b0), .in_18(1'b0), .in_19(1'b0),
    .in_20(1'b0), .in_21(1'b0), .in_22(1'b0), .in_23(1'b0), .in_24(1'b0), .in_25(1'b0), .in_26(1'b0),
    .in_27(1'b0), .in_28(1'b0), .in_29(1'b0), .in_30(1'b0), .in_31(1'b0), .out(O_4_0[2]));
  Multiplexer #(.Selector_Bits(5)) multiplexer_6 (
    .sel(B_4_0), .in_0(A_4_0[1]), .in_1(A_4_0[2]), .in_2(A_4_0[3]), .in_3(A_4_0[4]), .in_4(1'b0),
    .in_5(1'b0), .in_6(1'b0), .in_7(1'b0), .in_8(1'b0), .in_9(1'b0), .in_10(1'b0), .in_11(1'b0),
    .in_12(1'b0), .in_13(1'b0), .in_14(1'b0), .in_15(1'b0), .in_16(1'b0), .in_17(1'b0), .in_18(1'b0),
    .in_19(1'b0), .in_20(1'b0), .in_21(1'b0), .in_22(1'b0), .in_23(1'b0), .in_24(1'b0), .in_25(1'b0),
    .in_26(1'b0), .in_27(1'b0), .in_28(1'b0), .in_29(1'b0), .in_30(1'b0), .in_31(1'b0), .out(O_4_0[1]));
  Multiplexer #(.Selector_Bits(5)) multiplexer_7 (
    .sel(B_4_0), .in_0(A_4_0[0]), .in_1(A_4_0[1]), .in_2(A_4_0[2]), .in_3(A_4_0[3]), .in_4(A_4_0[4]),
    .in_5(1'b0), .in_6(1'b0), .in_7(1'b0), .in_8(1'b0), .in_9(1'b0), .in_10(1'b0), .in_11(1'b0),
    .in_12(1'b0), .in_13(1'b0), .in_14(1'b0), .in_15(1'b0), .in_16(1'b0), .in_17(1'b0), .in_18(1'b0),
    .in_19(1'b0), .in_20(1'b0), .in_21(1'b0), .in_22(1'b0), .in_23(1'b0), .in_24(1'b0), .in_25(1'b0),
    .in_26(1'b0), .in_27(1'b0), .in_28(1'b0), .in_29(1'b0), .in_30(1'b0), .in_31(1'b0), .out(O_4_0[0]));
  and and_1 (ZF, ~O_4_0[4], ~O_4_0[3], ~O_4_0[2], ~O_4_0[1], ~O_4_0[0]);  // And

  assign SF = O_4_0[4];

  // Other names for the same wires on the sheet: A0 = A_4_0[0]; A1 = A_4_0[1]; A2 = A_4_0[2]; A3 = A_4_0[3];
  //   A4 = A_4_0[4]; Sel[4:0] = B_4_0
endmodule
