// Digital circuit 5_Bit_CPU.dig as structural Verilog
module _5_Bit_CPU (
  input  [2:0] WA_2_0,
  input  [16:0] WD_16_0,
  input  WE,
  input  CLK,
  input  PC_EN,
  output [16:0] RD2_16_0,
  output [4:0] O_4_0
);

  wire _5_bit_alu_1_cf, _5_bit_alu_1_sf, _5_bit_alu_1_zf, control_unit_1_imm_sel, control_unit_1_jmp_sel,
       control_unit_1_reg_en, CPU_CLK, flag_register_1_cf, flag_register_1_sf, flag_register_1_zf;
  wire [0:0] R2;
  wire [1:0] op;
  wire [2:0] _3_bit_pc_adder_1_o_2_0, _3_bit_program_register_1_o_2_0, jmp_data, multiplexer_1_out;
  wire [4:0] _5_bit_register_set_with_4_register_1_a_4_0, _5_bit_register_set_with_4_register_1_b_4_0,
       multiplexer_2_out;
  wire [8:0] Don_t_Care;
  wire [16:13] _7x17_ram_1_rd1_16_0;

  Multiplexer #(.Bits(3)) multiplexer_1 (
    .sel(control_unit_1_jmp_sel), .in_0(_3_bit_pc_adder_1_o_2_0), .in_1(jmp_data), .out(multiplexer_1_out));
  _3_Bit_Program_Register _3_bit_program_register_1 (
    .CLK(CPU_CLK), .I_2_0(multiplexer_1_out), .O_2_0(_3_bit_program_register_1_o_2_0));
  _3_Bit_Pc_Adder _3_bit_pc_adder_1 (.I_2_0(_3_bit_program_register_1_o_2_0), .O_2_0(_3_bit_pc_adder_1_o_2_0));
  and and_1 (CPU_CLK, PC_EN, CLK);
  _7x17_RAM _7x17_ram_1 (
    .RA1_2_0(_3_bit_program_register_1_o_2_0), .RA2_2_0(3'b000), .WA_2_0(WA_2_0), .WD_16_0(WD_16_0), .WE(WE),
    .CLK(CLK), .RD1_16_0({_7x17_ram_1_rd1_16_0, jmp_data, R2[0], Don_t_Care}), .RD2_16_0(RD2_16_0));
  _5_Bit_Register_Set_with_4_Register _5_bit_register_set_with_4_register_1 (
    .WR_1_0(jmp_data[2:1]), .CLK(CPU_CLK), .WRD_4_0(O_4_0), .WE(control_unit_1_reg_en),
    .Ra_1_0(jmp_data[2:1]), .Rb_1_0({jmp_data[0], R2[0]}),
    .A_4_0(_5_bit_register_set_with_4_register_1_a_4_0), .B_4_0(_5_bit_register_set_with_4_register_1_b_4_0));
  _5_Bit_ALU _5_bit_alu_1 (
    .A_4_0(_5_bit_register_set_with_4_register_1_a_4_0), .B_4_0(multiplexer_2_out), .CF(_5_bit_alu_1_cf),
    .ZF(_5_bit_alu_1_zf), .SF(_5_bit_alu_1_sf), .OP_1_0(op), .CF_in(_5_bit_alu_1_cf), .O_4_0(O_4_0));
  Flag_Register flag_register_1 (
    .CF(flag_register_1_cf), .ZF(flag_register_1_zf), .SF(flag_register_1_sf), .CLK(CPU_CLK),
    .CF_i(_5_bit_alu_1_cf), .ZF_i(_5_bit_alu_1_zf), .SF_i(_5_bit_alu_1_sf));
  Control_Unit control_unit_1 (
    .opcode__3_0(_7x17_ram_1_rd1_16_0), .jmp_sel(control_unit_1_jmp_sel), .op__1_0(op),
    .CF(flag_register_1_cf), .SF(flag_register_1_sf), .ZF(flag_register_1_zf),
    .imm_sel(control_unit_1_imm_sel), .reg_en(control_unit_1_reg_en));
  Multiplexer #(.Bits(5)) multiplexer_2 (
    .sel(control_unit_1_imm_sel), .in_0(_5_bit_register_set_with_4_register_1_b_4_0),
    .in_1({jmp_data[0], R2[0], Don_t_Care[8:6]}), .out(multiplexer_2_out));

  // Other names for the same wires on the sheet: R2[1] = jmp_data[0]; R1[1:0] = jmp_data[2:1]; RD2[16:0] = RD2_16_0;
  //   WA[2:0] = WA_2_0; WD[16:0] = WD_16_0

  // Notes on the sheet:
  //   Register Mode (Type of op=00)=2bit(Type of op)+ 2bit(no of op)+ 3bit(Reg1) + 3bit(Reg2) + 7bit( don't care)
  //   Immediate Mode (Type of op=01)=2bit(Type of op)+ 2bit(no of op)+ 3bit(Reg1) + 5bit(Imm value)+ 5 bit(don't care)
  //   AND(op=00), ADD(op=01), SHR(op=10)
  //   AND R1,R1 -> 00000010010000000
  //   ADD R1,5   -> 01010100101000000
  //   ADD R2,4   -> 01010100010000000
  //   ADD R1,R2-> 00010010100000000
  //   SHR R1,4   -> 01100010010000000
  //   ADD R1,R1-> 00010010010000000
endmodule
