// Digital circuit Control Unit.dig as structural Verilog
module Control_Unit (
  input  [3:0] opcode__3_0,
  input  CF,
  input  SF,
  input  ZF,
  output [1:0] op__1_0,
  output imm_sel,
  output jmp_sel,
  output reg_en
);

  wire and_1_out, and_2_out, and_3_out, and_4_out, and_6_out, or_1_out;

  and and_1 (and_1_out, ~SF, ~ZF);  // And
  and and_2 (and_2_out, and_1_out, opcode__3_0[0], ~opcode__3_0[1]);  // And
  and and_3 (and_3_out, ~opcode__3_0[1], ~opcode__3_0[0]);  // And
  and and_4 (and_4_out, ~opcode__3_0[2], opcode__3_0[3]);  // And
  and and_5 (imm_sel, opcode__3_0[2], ~opcode__3_0[3]);  // And
  and and_6 (and_6_out, ~opcode__3_0[2], ~opcode__3_0[3]);  // And
  or or_1 (or_1_out, and_2_out, and_3_out);
  or or_2 (reg_en, imm_sel, and_6_out);
  and and_7 (jmp_sel, or_1_out, and_4_out);

  assign op__1_0 = opcode__3_0[1:0];
endmodule
