// Digital circuit Flag Register.dig as structural Verilog
module Flag_Register (
  input  CLK,
  input  ZF_i,
  input  CF_i,
  input  SF_i,
  output SF,
  output ZF,
  output CF
);

  _1_Bit_Reg _1_bit_reg_1 (.Din(CF_i), .Sel(1'b1), .CLK(CLK), .Dout(CF));
  _1_Bit_Reg _1_bit_reg_2 (.Din(ZF_i), .Sel(1'b1), .CLK(CLK), .Dout(ZF));
  _1_Bit_Reg _1_bit_reg_3 (.Din(SF_i), .Sel(1'b1), .CLK(CLK), .Dout(SF));
endmodule
